# Fritzing sketch D1 mini wristband (saved by Fritzing 0.9.3b)

parts:
  WeMos_D1_Mini_Battery_Shield1 = WeMos D1 Mini Battery Shield  # not connected
  WeMos_D1_Mini_Micro_SD_Shield1 = WeMos D1 Mini Micro SD Shield
  WeMos_D1_Mini_Dual_Base_Shield1 = WeMos D1 Mini Dual Base Shield  # not connected
  WeMos_D1_Mini_Protoboard_Shield1 = WeMos D1 Mini Protoboard Shield
  WeMos_D1_Mini1 = WeMos D1 Mini
  Part1 = InvenSense MPU6050
  R1 = Resistor [tolerance=±5% resistance=10k package="1206 [SMD]"]
  D1 = Rectifier Diode [part_number=1N4001 package="Melf DO-213 AB [SMD]"]
  D2 = Rectifier Diode [part_number=1N4001 package="Melf DO-213 AB [SMD]"]

nets:
  N1: WeMos_D1_Mini_Micro_SD_Shield1.D1, WeMos_D1_Mini1.D1
  N2: WeMos_D1_Mini_Micro_SD_Shield1.D2, WeMos_D1_Mini1.D2
  N3: WeMos_D1_Mini_Micro_SD_Shield1.D5, WeMos_D1_Mini1.D5
  N4: WeMos_D1_Mini_Micro_SD_Shield1.D6, WeMos_D1_Mini1.D6
  N5: WeMos_D1_Mini_Micro_SD_Shield1.D7, WeMos_D1_Mini1.D7
  N6: WeMos_D1_Mini_Micro_SD_Shield1.D8, WeMos_D1_Mini1.D8
  N7: WeMos_D1_Mini_Protoboard_Shield1.3V3, R1.Pin_1
  N8: WeMos_D1_Mini_Protoboard_Shield1.A0, WeMos_D1_Mini1.A0
  N9: WeMos_D1_Mini_Protoboard_Shield1.D1, Part1.SCL
  N10: WeMos_D1_Mini_Protoboard_Shield1.D2, Part1.SDA
  N11: WeMos_D1_Mini_Protoboard_Shield1.D3, D1.anode
  N12: WeMos_D1_Mini_Protoboard_Shield1.D4, D2.anode
  N13: WeMos_D1_Mini_Protoboard_Shield1.G, Part1.GND
  N14: Part1.VCC, R1.Pin_0

notes:
  analog:
  - heart rate
  - galvanic skin response
  - temperature?
