# Fritzing sketch D1 mini (saved by Fritzing 0.9.3b)
breadboards: 1

parts:
  WeMos_D1_Mini1 = WeMos D1 Mini
  D2 = Rectifier Diode [part_number=1N4001 package="300 mil [THT]"]
  D1 = Rectifier Diode [part_number=1N4001 package="300 mil [THT]"]
  Photoresistor = Photocell (LDR) [package=THT]
  PIR_Sensor_(H_jumper_trigger) = HC-SR501 Body Sensor Module
  R2 = Resistor [tolerance=±5% resistance=10k package="0603 [SMD]"]
  BMP280 = Adafruit_BMP280
  Microphone = Breakout Board for Electret Microphone
  Part1 = BME280 Breakout  # not connected

nets:
  N1: WeMos_D1_Mini1.G, PIR_Sensor_(H_jumper_trigger).GND
  N2: D2.cathode, D1.cathode
  N3: D2.anode, Microphone.AUD
  N4: D1.anode, Photoresistor.pin_1, R2.Pin_0
  GND: R2.Pin_1, BMP280.GND, Microphone.GND
  N5: BMP280.VIN, BMP280.SDO/ADR

custom parts:
  HC-SR501 Body Sensor Module: Pyroelectric Infrared PIR Motion Sensor Detector Module
  Adafruit_BMP280: Bosch has stepped up their game with their new BMP280 sensor, an environmental sensor with temperature, barometric pressure that is the next generation upgrade to the BMP085/BMP180/BMP183. This sensor is great for all sorts of weather sensing and can even be used in both I2C and SPI! This precision sensor from Bosch is the best low-cost, precision sensing solution for measuring barometric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
