# Fritzing sketch Nano version (saved by Fritzing 0.9.3b)
breadboards: 1

parts:
  Arduino_Nano = Arduino Nano (Rev3.0)
  Microphone = Breakout Board for Electret Microphone
  BMP280 = Adafruit_BMP280
  Photoresistor = Photocell (LDR) [package=THT]
  R2 = Resistor [tolerance=±5% resistance=10k package="0603 [SMD]"]
  PIR_Sensor_(H_jumper_-_adjusment_maximum_counter-clockwise) = HC-SR501 Body Sensor Module

nets:
  GND: Arduino_Nano.GND, Microphone.GND, BMP280.GND, R2.Pin_1, PIR_Sensor_(H_jumper_-_adjusment_maximum_counter-clockwise).GND
  N1: Arduino_Nano.D2, PIR_Sensor_(H_jumper_-_adjusment_maximum_counter-clockwise).OUT
  5V: Arduino_Nano.5V, Photoresistor.pin_0, PIR_Sensor_(H_jumper_-_adjusment_maximum_counter-clockwise).VCC
  N2: Arduino_Nano.A5, BMP280.SCK/SCL
  N3: Arduino_Nano.A4, BMP280.SDI/SDA
  N4: Arduino_Nano.A1, Photoresistor.pin_1, R2.Pin_0
  N5: Arduino_Nano.A0, Microphone.AUD
  3V3: Arduino_Nano.3V3, Microphone.VCC, BMP280.VIN, BMP280.SDO/ADR

custom parts:
  Adafruit_BMP280: Bosch has stepped up their game with their new BMP280 sensor, an environmental sensor with temperature, barometric pressure that is the next generation upgrade to the BMP085/BMP180/BMP183. This sensor is great for all sorts of weather sensing and can even be used in both I2C and SPI! This precision sensor from Bosch is the best low-cost, precision sensing solution for measuring barometric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
  HC-SR501 Body Sensor Module: Pyroelectric Infrared PIR Motion Sensor Detector Module
